// Logisim project whole_circuit_23097881.circ as structural Verilog: 1 circuit, main circuit main
module main (
);

  wire and_1_out, and_2_out, and_3_out, and_4_out, and_5_out, and_6_out, and_7_out, and_8_out, and_9_out,
       and_10_out, and_11_out, and_12_out, and_13_out, and_14_out, and_15_out, and_16_out, button_1_out,
       button_2_out, button_3_out, button_4_out, button_5_out, button_6_out, button_7_out, button_8_out,
       not_1_out, not_2_out, not_3_out, not_4_out, not_5_out, not_6_out, not_7_out, not_8_out, not_9_out,
       not_10_out, not_11_out, not_12_out, not_13_out, not_14_out, not_15_out, not_16_out, not_17_out,
       not_18_out, not_19_out, not_20_out, not_21_out, or_1_out, or_2_out, or_3_out, or_4_out, or_5_out,
       or_6_out, or_7_out;
  wire [2:0] priority_encoder_1_out;

  Button button_1 (.out(button_1_out));
  Button button_2 (.out(button_2_out));
  Button button_3 (.out(button_3_out));
  Button button_4 (.out(button_4_out));
  Button button_5 (.out(button_5_out));
  Button button_6 (.out(button_6_out));
  Button button_7 (.out(button_7_out));
  Button button_8 (.out(button_8_out));
  Priority_Encoder priority_encoder_1 (
    .in0(button_1_out), .in1(button_2_out), .in2(button_3_out), .in3(button_4_out), .in4(button_5_out),
    .in5(button_6_out), .in6(button_7_out), .in7(button_8_out), .out(priority_encoder_1_out));  // open: en_in, gs, en_out
  not not_1 (not_1_out, priority_encoder_1_out[1]);
  not not_2 (not_2_out, priority_encoder_1_out[2]);
  not not_3 (not_3_out, priority_encoder_1_out[0]);
  not not_4 (not_4_out, priority_encoder_1_out[1]);
  not not_5 (not_5_out, priority_encoder_1_out[1]);
  not not_6 (not_6_out, priority_encoder_1_out[0]);
  not not_7 (not_7_out, priority_encoder_1_out[1]);
  not not_8 (not_8_out, priority_encoder_1_out[0]);
  not not_9 (not_9_out, priority_encoder_1_out[0]);
  not not_10 (not_10_out, priority_encoder_1_out[2]);
  not not_11 (not_11_out, priority_encoder_1_out[0]);
  not not_12 (not_12_out, priority_encoder_1_out[1]);
  not not_13 (not_13_out, priority_encoder_1_out[0]);
  and and_1 (and_1_out, not_13_out, not_14_out);
  not not_14 (not_14_out, priority_encoder_1_out[2]);
  not not_15 (not_15_out, priority_encoder_1_out[0]);
  and and_2 (and_2_out, not_15_out, priority_encoder_1_out[1]);
  not not_16 (not_16_out, priority_encoder_1_out[1]);
  and and_3 (and_3_out, not_16_out, priority_encoder_1_out[0], priority_encoder_1_out[2]);
  not not_17 (not_17_out, priority_encoder_1_out[2]);
  and and_4 (and_4_out, not_17_out, priority_encoder_1_out[1]);
  and and_5 (and_5_out, priority_encoder_1_out[1], not_18_out);
  not not_18 (not_18_out, priority_encoder_1_out[0]);
  not not_19 (not_19_out, priority_encoder_1_out[2]);
  and and_6 (and_6_out, not_19_out, not_20_out);
  not not_20 (not_20_out, priority_encoder_1_out[0]);
  and and_7 (and_7_out, not_2_out, priority_encoder_1_out[1]);
  and and_8 (and_8_out, priority_encoder_1_out[2], not_3_out);
  and and_9 (and_9_out, priority_encoder_1_out[2], not_4_out);
  and and_10 (and_10_out, priority_encoder_1_out[2], not_5_out);
  and and_11 (and_11_out, priority_encoder_1_out[2], not_6_out);
  and and_12 (and_12_out, not_7_out, not_8_out);
  and and_13 (and_13_out, not_9_out, not_10_out);
  and and_14 (and_14_out, priority_encoder_1_out[0], priority_encoder_1_out[2]);
  not not_21 (not_21_out, priority_encoder_1_out[2]);
  and and_15 (and_15_out, not_11_out, not_12_out);
  and and_16 (and_16_out, priority_encoder_1_out[0], priority_encoder_1_out[1]);
  or or_1 (or_1_out, and_10_out, and_11_out, and_12_out);
  or or_2 (or_2_out, priority_encoder_1_out[1], and_13_out, and_14_out);
  or or_3 (or_3_out, not_21_out, and_15_out, and_16_out);
  or or_4 (or_4_out, and_1_out, and_2_out);
  or or_5 (or_5_out, and_3_out, and_4_out, and_5_out, and_6_out);
  or or_6 (or_6_out, priority_encoder_1_out[2], not_1_out, priority_encoder_1_out[0]);
  or or_7 (or_7_out, and_7_out, and_8_out, and_9_out);
  _7_Segment_Display u_7_segment_display_1 (
    .g(or_7_out), .f(or_1_out), .a(or_2_out), .b(or_3_out), .e(or_4_out), .d(or_5_out), .c(or_6_out));  // open: dp

  // Notes on the sheet:
  //   S1
  //   S2
  //   S3
  //   S4
endmodule
